# Fritzing sketch Untitled Sketch (saved by Fritzing 0.9.10b)
breadboards: 1

parts:
  HC-SR04_Sensor_1 = HC-SR04 Ultrasonic Distance Sensor
  부품1 = Arduino Mega 2560 (Rev3)

nets:
  VCC: HC-SR04_Sensor_1.VCC, 부품1.5V
  N1: HC-SR04_Sensor_1.TRIG, 부품1.D22
  N2: HC-SR04_Sensor_1.ECHO, 부품1.D23
  GND: HC-SR04_Sensor_1.GND, 부품1.GND
