# Fritzing sketch sonar1 (saved by Fritzing 0.9.10b)
breadboards: 1

parts:
  HC-SR04_Sensor_1 = HC-SR04 Ultrasonic Distance Sensor
  부품1 = Arduino Mega 2560 (Rev3)
  S1 = H-Bridge with L298N  # not connected

nets:
  VCC: HC-SR04_Sensor_1.VCC, 부품1.5V
  N1: HC-SR04_Sensor_1.TRIG, 부품1.D3_PWM
  N2: HC-SR04_Sensor_1.ECHO, 부품1.D4_PWM
  GND: HC-SR04_Sensor_1.GND, 부품1.GND

custom parts:
  H-Bridge with L298N: h-bridge
